# Fritzing sketch Water Shed Controller (saved by Fritzing 0.9.2b)
breadboards: 1

parts:
  Part1 = Adafruit Feather M0 RFM9x LoRa [part_number="Adafruit #3178 or #3179"]
  Part2 = SRF05 Ultrasonic Rangefinder
  Part3 = SRF05 Ultrasonic Rangefinder
  DHT1 = DHT22 Humidity and Temperature Sensor
  KY-2 = Keyes Relay [package=THT]
  R2 = Resistor [tolerance=±5% resistance=1k package="0603 [SMD]"]
  R6 = Resistor [tolerance=±5% resistance=1k package="0603 [SMD]"]
  R7 = Resistor [tolerance=±5% resistance=1k package="0603 [SMD]"]
  R8 = Resistor [tolerance=±5% resistance=1k package="0603 [SMD]"]
  R11 = Resistor [tolerance=±5% resistance=10k package="0603 [SMD]"]

nets:
  N1: Part1.A0, KY-2.signal
  GND: Part1.GND, Part2.Echo, Part3.GND, DHT1.GND, KY-2.ground, R7.Pin_1, R8.Pin_0
  VCC: Part1.VBUS, Part3.VCC, DHT1.VDD, KY-2.power, R11.Pin_0
  N2: Part1.D13, Part3.Trig
  N3: Part1.D12, R2.Pin_0, R7.Pin_0
  N4: Part1.D11, Part2.VCC
  N5: Part1.D10, R6.Pin_0, R8.Pin_1
  N6: Part1.D9, DHT1.DATA, R11.Pin_1
  N7: Part2.Trig, R6.Pin_1
  N8: Part3.Echo, R2.Pin_1

notes:
  5V Rail

custom parts:
  Adafruit Feather M0 RFM9x LoRa: This is the Adafruit Feather M0 RFM95 LoRa Radio - our take on an microcontroller with a "Long Range (LoRa)" packet radio transceiver with built in USB and battery charging. Its an Adafruit Feather M0 with a 433Mhz or 900MHz radio module cooked in! Great for making wireless networks that are more flexible than Bluetooth LE and without the high power requirements of WiFi. We have other boards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
  Keyes Relay: The Keyes 5V relay module is suitable for SCM development, home appliance control. It uses a 5V~12V TIL control signal which can control DC / AC signal.
